// Logisim project IT012_Lab01_23520968.circ as structural Verilog
module Warmup (
  input  A,
  input  B,
  output F
);

  wire NOT_out;

  not NOT (NOT_out, B);
  and AND2 (F, A, NOT_out);
endmodule

module TN1 (
  input  A,
  input  B,
  input  C,
  output F_NOT,
  output F_AND,
  output F_OR,
  output F_NAND,
  output F_NOR,
  output F_XOR,
  output F_XNOR,
  output XOR3,
  output NAND3,
  output CHAIN
);

  wire NAND2_2_out;

  not NOT (F_NOT, A);
  and AND2 (F_AND, A, B);
  or OR2 (F_OR, A, B);
  nand NAND2 (F_NAND, A, B);
  nor NOR2 (F_NOR, A, B);
  xor XOR2 (F_XOR, A, B);
  xnor XNOR2 (F_XNOR, A, B);
  ExactlyOne u_XOR3 (.out(XOR3), .in0(A), .in1(B), .in2(C));
  nand u_NAND3 (NAND3, A, B, C);
  nand NAND2_2 (NAND2_2_out, A, B);
  nand NAND2_3 (CHAIN, NAND2_2_out, C);
endmodule

module TN2 (
  input  x,
  input  y,
  input  z,
  output EQ1,
  output EQ2,
  output EQ3,
  output EQ4,
  output EQ5
);

  wire AND2_2_out, AND2_3_out, AND2_4_out, AND2_out, NAND2_out, NOR2_out, OR2_2_out, OR2_3_out, OR2_4_out,
       OR2_5_out, OR2_out;

  and AND2 (AND2_out, y, z);
  or OR2 (OR2_out, x, y);
  or OR2_2 (OR2_2_out, x, z);
  and AND2_2 (AND2_2_out, ~x, y);  // AND_Gate
  nor NOR2 (NOR2_out, x, y);
  and AND2_3 (AND2_3_out, ~x, ~y);  // AND_Gate
  nand NAND2 (NAND2_out, x, y);
  or OR2_3 (OR2_3_out, x, AND2_out);
  and AND2_4 (AND2_4_out, OR2_out, OR2_2_out);
  or OR2_4 (OR2_4_out, x, AND2_2_out);
  or OR2_5 (OR2_5_out, x, y);
  xnor XNOR2 (EQ1, NOR2_out, AND2_3_out);
  xnor XNOR2_2 (EQ2, NAND2_out, AND2_3_out);
  xnor XNOR2_3 (EQ3, OR2_3_out, AND2_4_out);
  xnor XNOR2_4 (EQ4, x, OR2_4_out);
  xnor XNOR2_5 (EQ5, OR2_4_out, OR2_5_out);
endmodule

module TN3 (
  input  A,
  input  B,
  input  C,
  input  D,
  output F
);

  wire AND4_2_out, AND4_3_out, AND4_4_out, AND4_5_out, AND4_6_out, AND4_out, NOT_2_out, NOT_3_out, NOT_4_out,
       NOT_out;

  and AND4 (AND4_out, NOT_out, NOT_2_out, C, NOT_4_out);
  and AND4_2 (AND4_2_out, NOT_out, NOT_2_out, C, D);
  and AND4_3 (AND4_3_out, NOT_out, B, NOT_3_out, D);
  or OR6 (F, AND4_out, AND4_2_out, AND4_3_out, AND4_4_out, AND4_5_out, AND4_6_out);
  and AND4_4 (AND4_4_out, NOT_out, B, C, D);
  and AND4_5 (AND4_5_out, A, NOT_2_out, C, D);
  and AND4_6 (AND4_6_out, A, B, NOT_3_out, D);
  not NOT (NOT_out, A);
  not NOT_2 (NOT_2_out, B);
  not NOT_3 (NOT_3_out, C);
  not NOT_4 (NOT_4_out, D);
endmodule

module TN4 (
  input  A,
  input  B,
  input  C,
  input  D,
  output EQ1,
  output EQ2
);

  wire AND3_2_out, AND3_3_out, AND3_4_out, AND3_out, AND4_2_out, AND4_3_out, AND4_4_out, AND4_5_out,
       AND4_6_out, AND4_out, AND5_out, NOT_2_out, NOT_3_out, NOT_4_out, NOT_out, OR2_2_out, OR2_3_out,
       OR2_4_out, OR2_out, OR3_out, OR4_out, OR6_out;

  and AND4 (AND4_out, NOT_2_out, NOT_out, C, NOT_3_out);
  and AND4_2 (AND4_2_out, NOT_2_out, NOT_out, C, D);
  and AND4_3 (AND4_3_out, NOT_2_out, B, NOT_4_out, D);
  or OR6 (OR6_out, AND4_out, AND4_2_out, AND4_3_out, AND4_4_out, AND4_5_out, AND4_6_out);
  and AND4_4 (AND4_4_out, NOT_2_out, B, C, D);
  and AND4_5 (AND4_5_out, A, NOT_out, C, D);
  and AND4_6 (AND4_6_out, A, B, NOT_4_out, D);
  xnor XNOR2 (EQ1, OR6_out, OR4_out);
  and AND3 (AND3_out, NOT_2_out, NOT_out, C);
  and AND3_2 (AND3_2_out, NOT_2_out, B, D);
  or OR4 (OR4_out, AND3_out, AND3_2_out, AND3_3_out, AND3_4_out);
  and AND3_3 (AND3_3_out, B, NOT_4_out, D);
  and AND3_4 (AND3_4_out, NOT_out, C, D);
  xnor XNOR2_2 (EQ2, OR4_out, AND5_out);
  or OR2 (OR2_out, C, D);
  or OR2_2 (OR2_2_out, B, C);
  or OR2_3 (OR2_3_out, NOT_out, D);
  and AND5 (AND5_out, OR2_out, OR2_2_out, OR2_3_out, OR2_4_out, OR3_out);
  not NOT (NOT_out, B);
  not NOT_2 (NOT_2_out, A);
  or OR2_4 (OR2_4_out, NOT_2_out, D);
  not NOT_3 (NOT_3_out, D);
  not NOT_4 (NOT_4_out, C);
  or OR3 (OR3_out, NOT_2_out, NOT_out, NOT_4_out);
endmodule

module TN5 (
  input  A,
  input  B,
  input  C,
  output F
);

  wire XOR2_out;

  xor XOR2 (XOR2_out, A, B);
  xor XOR2_2 (F, XOR2_out, C);
endmodule
