// Logisim project IT012_Lab02_23520968.circ as structural Verilog
module Warmup (
  input  [7:0] A,
  input  [7:0] B,
  output [7:0] S
);

  Adder adder_1 (.a(A), .b(B), .out(S));  // open: cin, cout
  // Probe on S
endmodule

module FA (
  input  A,
  input  B,
  input  Cin,
  output S,
  output Cout
);

  wire AND2_2_out, AND2_out, XOR2_out;

  xor XOR2 (XOR2_out, A, B);
  and AND2 (AND2_out, A, B);
  xor XOR2_2 (S, XOR2_out, Cin);
  and AND2_2 (AND2_2_out, XOR2_out, Cin);
  or OR2 (Cout, AND2_out, AND2_2_out);
endmodule

module ADDSUB4 (
  input  [3:0] A,
  input  [3:0] B,
  input  SUB,
  output Z,
  output [3:0] S,
  output C,
  output N,
  output V
);

  wire fa_1_cout, fa_2_cout, fa_3_cout, XOR2_2_out, XOR2_3_out, XOR2_4_out, XOR2_5_out, XOR2_6_out, XOR2_out;

  xor XOR2 (XOR2_out, B[0], SUB);
  xor XOR2_2 (XOR2_2_out, B[1], SUB);
  xor XOR2_3 (XOR2_3_out, B[2], SUB);
  xor XOR2_4 (XOR2_4_out, B[3], SUB);
  FA fa_1 (.A(A[0]), .B(XOR2_out), .Cin(SUB), .S(S[0]), .Cout(fa_1_cout));
  FA fa_2 (.A(A[1]), .B(XOR2_2_out), .Cin(fa_1_cout), .S(S[1]), .Cout(fa_2_cout));
  // Probe on fa_1_cout
  FA fa_3 (.A(A[2]), .B(XOR2_3_out), .Cin(fa_2_cout), .S(S[2]), .Cout(fa_3_cout));
  // Probe on fa_2_cout
  // Probe on fa_3_cout
  FA fa_4 (.A(A[3]), .B(XOR2_4_out), .Cin(fa_3_cout), .S(N), .Cout(C));
  nor u_Z (Z, N, S[2], S[1], S[0]);
  xor XOR2_5 (XOR2_5_out, N, A[3]);
  xor XOR2_6 (XOR2_6_out, N, XOR2_4_out);
  and AND2 (V, XOR2_5_out, XOR2_6_out);

  assign S[3] = N;
endmodule

module ALU8 (
  input  [7:0] A,
  input  [2:0] OP,
  input  [7:0] B,
  output [7:0] R,
  output Z,
  output LT
);

  wire [7:0] adder_1_out, adder_2_out, AND2_out, multiplexer_1_out, multiplexer_2_out, NOT_out, OR2_out,
       subtractor_1_out, subtractor_2_out, XOR2_out;

  Adder adder_1 (.a(A), .b(B), .out(adder_1_out));  // open: cin, cout
  Adder adder_2 (.a(A), .b(8'h1), .out(adder_2_out));  // open: cin, cout
  Subtractor subtractor_1 (.a(A), .b(B), .out(subtractor_1_out));  // open: bin, bout
  Subtractor subtractor_2 (.a(A), .b(8'h1), .out(subtractor_2_out));  // open: bin, bout
  assign AND2_out = A & B;  // AND_Gate AND2, 8 bits wide
  assign OR2_out = A | B;  // OR_Gate OR2, 8 bits wide
  assign NOT_out = ~A;  // NOT_Gate NOT, 8 bits wide
  assign XOR2_out = A ^ B;  // XOR_Gate XOR2, 8 bits wide
  Multiplexer #(.select(2), .width(8)) multiplexer_1 (
    .in0(adder_1_out), .in1(adder_2_out), .in2(subtractor_1_out), .in3(subtractor_2_out),
    .out(multiplexer_1_out), .sel(OP[1:0]));  // open: en
  Multiplexer #(.select(2), .width(8)) multiplexer_2 (
    .in0(AND2_out), .in1(OR2_out), .in2(NOT_out), .in3(XOR2_out), .out(multiplexer_2_out), .sel(OP[1:0]));  // open: en
  Multiplexer #(.width(8)) multiplexer_3 (
    .in0(multiplexer_1_out), .in1(multiplexer_2_out), .out(R), .sel(OP[2]));  // open: en
  nor nor_1 (Z, R[0], R[1], R[2], R[3], R[4], R[5], R[6], R[7]);
  LT u_LT (.A7(A[7]), .B7(B[7]), .R7(R[7]), .LT(LT));
endmodule

module LT (
  input  A7,
  input  B7,
  input  R7,
  output LT
);

  wire AND2_2_out, AND2_3_out, AND2_out, NOT_out;

  not NOT (NOT_out, B7);
  and AND2 (AND2_out, A7, NOT_out);
  and AND2_2 (AND2_2_out, R7, NOT_out);
  and AND2_3 (AND2_3_out, A7, R7);
  or OR3 (LT, AND2_out, AND2_2_out, AND2_3_out);
endmodule

module DLATCH (
  input  E,
  input  D,
  output Q
);

  Multiplexer multiplexer_1 (.in0(Q), .in1(D), .out(Q), .sel(E));  // open: en
endmodule

module TN3 (
  input  CLK,
  input  D,
  output Q1,
  output Q2,
  output Q3
);

  wire D_Flipflop_q, DLATCH_q;

  DLATCH DLATCH (.D(D), .E(CLK), .Q(DLATCH_q));
  D_Flip_Flop D_Flipflop (.clk(CLK), .D(D), .Q(D_Flipflop_q));  // open: Qn, preset, en, reset
  DFF_MS DFF_MS (.D(D), .CLK(CLK), .Q3(Q3));
  DLATCH DLATCH_2 (.D(DLATCH_q), .E(CLK), .Q(Q1));
  D_Flip_Flop D_Flipflop_2 (.clk(CLK), .D(D_Flipflop_q), .Q(Q2));  // open: Qn, preset, en, reset
endmodule

module DFF_MS (
  input  CLK,
  input  D,
  output Q3
);

  wire D_LATCH_q, NOT_out;

  not NOT (NOT_out, CLK);
  DLATCH D_LATCH (.D(D), .E(NOT_out), .Q(D_LATCH_q));
  DLATCH D_LATCH_2 (.D(D_LATCH_q), .E(CLK), .Q(Q3));
endmodule

module REGFILE (
  input  [7:0] DIN,
  input  WE,
  input  [1:0] RD,
  input  [1:0] RA,
  input  [1:0] RB,
  input  CLK,
  output [7:0] QA,
  output [7:0] QB,
  output [7:0] R0,
  output [7:0] R1,
  output [7:0] R2,
  output [7:0] R3
);

  wire decoder_1_out0, decoder_1_out1, decoder_1_out2, decoder_1_out3;

  Decoder #(.select(2), .disabled(0)) decoder_1 (
    .out0(decoder_1_out0), .out1(decoder_1_out1), .out2(decoder_1_out2), .out3(decoder_1_out3), .sel(RD),
    .en(WE));
  Register u_R0 (.D(DIN), .en(decoder_1_out0), .Q(R0), .clk(CLK));  // open: clr
  Register u_R1 (.D(DIN), .en(decoder_1_out1), .Q(R1), .clk(CLK));  // open: clr
  Register u_R2 (.D(DIN), .en(decoder_1_out2), .Q(R2), .clk(CLK));  // open: clr
  Register u_R3 (.D(DIN), .en(decoder_1_out3), .Q(R3), .clk(CLK));  // open: clr
  Multiplexer #(.select(2), .width(8)) multiplexer_1 (
    .in0(R0), .in1(R1), .in2(R2), .in3(R3), .out(QA), .sel(RA));  // open: en
  Multiplexer #(.select(2), .width(8)) multiplexer_2 (
    .in0(R0), .in1(R1), .in2(R2), .in3(R3), .out(QB), .sel(RB));  // open: en
endmodule

module DATAPATH (
  input  [2:0] OP,
  input  WE,
  input  [1:0] RD,
  input  SRC,
  input  CLK,
  input  [1:0] RA,
  input  [1:0] RB,
  output Z,
  output [7:0] R0,
  output [7:0] R1,
  output [7:0] R2,
  output [7:0] R3
);

  wire [7:0] ALU8_r, multiplexer_1_out, regfile_1_qa, regfile_1_qb;

  REGFILE regfile_1 (
    .DIN(multiplexer_1_out), .WE(WE), .RD(RD), .CLK(CLK), .RA(RA), .RB(RB), .QA(regfile_1_qa),
    .QB(regfile_1_qb), .R0(R0), .R1(R1), .R2(R2), .R3(R3));
  ALU8 ALU8 (.A(regfile_1_qa), .B(regfile_1_qb), .OP(OP), .R(ALU8_r), .Z(Z));  // open: LT
  Multiplexer #(.width(8)) multiplexer_1 (.in0(ALU8_r), .in1(8'h7), .out(multiplexer_1_out), .sel(SRC));  // open: en
endmodule
